# Fritzing sketch Microhydroponics (saved by Fritzing 0.9.3b)
circuit board: 8.46667cm x 5.64444cm
breadboards: 1

parts:
  Part1 = Adafruit ADS1015 12Bit I2C ADC [part_number="Adafruit #1083"]
  Power_plug1 = Power plug
  MPX4250AP1 = MPX4250AP pressure sensor [part_number=MPX]
  R2 = Resistor [tolerance=±5% resistance=220 package=THT]
  R1 = Temperature Sensor (Thermistor) [thermistor_type=NTC package=THT]

nets:
  N1: Part1.AIN2, MPX4250AP1.V_out
  N2: Part1.AIN1, R2.Pin_1, R1.pin_0
  GND: Part1.GND, Power_plug1.GND, MPX4250AP1.GND, R1.pin_1
  VDD: Part1.VDD, Power_plug1.VCC, MPX4250AP1.Vs, R2.Pin_0

custom parts:
  Adafruit ADS1015 12Bit I2C ADC: For microcontrollers without an analog-to-digital converter or when you want a higher-precision ADC, the ADS1015 provides 12-bit precision at 3300 samples/second over I2C. The chip can be configured as 4 single-ended input channels, or two differential channels. As a nice bonus, it even includes a programmable gain amplifier, up to x16, to help boost up smaller single/differential signals to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
